# Fritzing sketch circuit_test_01 (saved by Fritzing 0.7.11b)
breadboards: 1

parts:
  Arduino1 = Arduino
  S1 = Pushbutton [package="[THT]"]  # not connected
  R1 = Rotary Potentiometer (Small) [maximum_resistance=100kΩ]
  LED1 = LED - 5mm [color="Red (633nm)" package="5 mm [THT]"]
  LED2 = LED - 5mm [color="Red (633nm)" package="5 mm [THT]"]  # not connected
  R2 = Resistor [tolerance=±5% resistance=220 package=THT]
  R3 = Resistor [tolerance=±5% resistance=220 package=THT]

nets:
  N1: Arduino1.D4, R3.Pin_1
  N2: Arduino1.+5V, R1.leg2
  N3: Arduino1.GND, R1.leg1, LED1.cathode
  N4: Arduino1.A0, R1.wiper
  N5: Arduino1.A5, R2.Pin_0
  N6: LED1.anode, R3.Pin_0
