# Fritzing sketch game_controller_sch (saved by Fritzing 0.7.11b)
breadboards: 1

parts:
  Arduino1 = Arduino
  LED1 = LED - 5mm [color="Red (633nm)" package="5 mm [THT]"]
  LED2 = LED - 5mm [color="Yellow (595nm)" package="5 mm [THT]"]
  LED3 = LED - 5mm [color="Red (633nm)" package="5 mm [THT]"]
  LED4 = LED - 5mm [color="Yellow (595nm)" package="5 mm [THT]"]
  R1 = Resistor [tolerance=±5% resistance=220 package=THT]
  R2 = Resistor [tolerance=±5% resistance=220 package=THT]
  R3 = Resistor [tolerance=±5% resistance=220 package=THT]
  R4 = Resistor [tolerance=±5% resistance=220 package=THT]
  R5 = Rotary Potentiometer (Small) [maximum_resistance=100kΩ]
  S1 = Pushbutton [package=THT]
  S2 = Pushbutton [package=THT]

nets:
  N1: Arduino1.GND, LED1.cathode, LED2.cathode, LED3.cathode, LED4.cathode, R5.leg1, S1.leg0, S2.leg0
  N2: Arduino1.D5, R4.Pin_1
  N3: Arduino1.D4, R3.Pin_1
  N4: Arduino1.D2, R2.Pin_1
  N5: Arduino1.D1TX, R1.Pin_1
  N6: Arduino1.+5V, R5.leg2
  N7: Arduino1.A0, R5.wiper
  N8: Arduino1.A1, S1.leg1
  N9: Arduino1.A2, S2.leg1
  N10: LED1.anode, R1.Pin_0
  N11: LED2.anode, R2.Pin_0
  N12: LED3.anode, R3.Pin_0
  N13: LED4.anode, R4.Pin_0
