# Fritzing sketch temp_test (saved by Fritzing 0.7.11b)
breadboards: 1

parts:
  Arduino1 = Arduino
  LED1 = LED - 5mm [color="Red (633nm)" package="5 mm [THT]"]
  LED2 = LED - 5mm [color="Yellow (595nm)" package="5 mm [THT]"]
  R1 = Resistor [tolerance=±5% resistance=10k package=THT]
  R2 = Resistor [tolerance=±5% resistance=10k package=THT]
  T1 = LM35 Temperature Sensor [package="TO92 [THT]"]

nets:
  N1: Arduino1.D3, R2.Pin_1
  N2: Arduino1.D2, R1.Pin_1
  N3: Arduino1.+5V, T1.+Vs
  GND: Arduino1.GND, LED1.cathode, LED2.cathode, T1.GND
  N4: Arduino1.A4, T1.Vout
  N5: LED1.anode, R1.Pin_0
  N6: LED2.anode, R2.Pin_0
